// Logisim project CORRECT_ODV-3.circ as structural Verilog: 1 circuit, main circuit main
module main (
  input  [7:0] in_1,
  input  [7:0] in_2,
  output [7:0] out_3
);

  wire and_1_out, and_2_out, and_3_out, and_4_out, and_5_out, and_6_out, and_7_out, and_8_out, and_9_out,
       and_10_out, and_11_out, and_12_out, and_13_out, and_14_out, and_15_out, and_16_out, and_17_out,
       and_18_out, and_19_out, and_20_out, and_21_out, and_22_out, and_23_out, and_24_out, and_25_out,
       and_26_out, and_27_out, and_28_out, and_29_out, and_30_out, and_31_out, and_32_out, not_1_out,
       not_2_out, not_3_out, not_4_out, not_5_out, not_6_out, not_7_out, not_8_out, not_9_out, not_10_out,
       not_11_out, not_12_out, not_13_out, not_14_out, not_15_out, not_16_out, not_17_out, not_18_out,
       not_19_out, not_20_out, not_21_out, not_22_out, not_23_out, not_24_out, not_25_out, not_26_out,
       not_27_out, not_28_out, not_29_out, not_30_out, not_31_out, not_32_out, not_33_out, not_34_out,
       not_35_out, not_36_out, not_37_out, not_38_out, not_39_out, not_40_out, not_41_out, not_42_out,
       not_43_out, not_44_out, not_45_out, not_46_out, not_47_out, not_48_out, or_1_out, or_2_out, or_4_out,
       or_5_out, or_6_out, or_8_out, or_9_out, or_10_out, or_12_out, or_13_out, or_14_out, or_16_out,
       or_17_out, or_18_out, or_20_out, or_21_out, or_22_out, or_24_out, or_25_out, or_26_out, or_28_out,
       or_29_out, or_30_out, xor_1_out, xor_2_out, xor_3_out, xor_4_out, xor_5_out, xor_6_out, xor_7_out,
       xor_8_out, xor_9_out, xor_10_out, xor_11_out, xor_12_out, xor_13_out, xor_14_out, xor_15_out,
       xor_16_out;

  not not_1 (not_1_out, in_1[0]);
  not not_2 (not_2_out, in_2[0]);
  xor xor_1 (xor_1_out, in_2[0], in_1[0]);
  xor xor_2 (xor_2_out, in_2[0], in_1[0]);
  or or_1 (or_1_out, not_1_out, in_2[0]);
  or or_2 (or_2_out, in_1[0], not_2_out);
  not not_3 (not_3_out, xor_1_out);
  not not_4 (not_4_out, 1'b0);
  not not_5 (not_5_out, or_2_out);
  not not_6 (not_6_out, 1'b0);
  and and_1 (and_1_out, not_3_out, 1'b0);
  and and_2 (and_2_out, xor_2_out, not_4_out);
  and and_3 (and_3_out, or_1_out, 1'b0);
  and and_4 (and_4_out, not_5_out, not_6_out);
  or or_3 (out_3[0], and_1_out, and_2_out);
  or or_4 (or_4_out, and_3_out, and_4_out);
  not not_7 (not_7_out, in_1[1]);
  not not_8 (not_8_out, in_2[1]);
  not not_9 (not_9_out, xor_3_out);
  xor xor_3 (xor_3_out, in_2[1], in_1[1]);
  xor xor_4 (xor_4_out, in_2[1], in_1[1]);
  not not_10 (not_10_out, or_4_out);
  or or_5 (or_5_out, not_7_out, in_2[1]);
  or or_6 (or_6_out, in_1[1], not_8_out);
  not not_11 (not_11_out, or_6_out);
  not not_12 (not_12_out, or_4_out);
  and and_5 (and_5_out, not_9_out, or_4_out);
  and and_6 (and_6_out, xor_4_out, not_10_out);
  and and_7 (and_7_out, or_5_out, or_4_out);
  and and_8 (and_8_out, not_11_out, not_12_out);
  or or_7 (out_3[1], and_5_out, and_6_out);
  or or_8 (or_8_out, and_7_out, and_8_out);
  xor xor_5 (xor_5_out, in_2[2], in_1[2]);
  xor xor_6 (xor_6_out, in_2[2], in_1[2]);
  not not_13 (not_13_out, in_1[2]);
  not not_14 (not_14_out, in_2[2]);
  not not_15 (not_15_out, xor_5_out);
  not not_16 (not_16_out, or_8_out);
  or or_9 (or_9_out, not_13_out, in_2[2]);
  or or_10 (or_10_out, in_1[2], not_14_out);
  not not_17 (not_17_out, or_10_out);
  not not_18 (not_18_out, or_8_out);
  and and_9 (and_9_out, not_15_out, or_8_out);
  and and_10 (and_10_out, xor_6_out, not_16_out);
  and and_11 (and_11_out, or_9_out, or_8_out);
  and and_12 (and_12_out, not_17_out, not_18_out);
  or or_11 (out_3[2], and_9_out, and_10_out);
  or or_12 (or_12_out, and_11_out, and_12_out);
  not not_19 (not_19_out, in_1[3]);
  not not_20 (not_20_out, in_2[3]);
  xor xor_7 (xor_7_out, in_2[3], in_1[3]);
  xor xor_8 (xor_8_out, in_2[3], in_1[3]);
  or or_13 (or_13_out, not_19_out, in_2[3]);
  or or_14 (or_14_out, in_1[3], not_20_out);
  not not_21 (not_21_out, xor_7_out);
  not not_22 (not_22_out, or_12_out);
  not not_23 (not_23_out, or_14_out);
  not not_24 (not_24_out, or_12_out);
  and and_13 (and_13_out, not_21_out, or_12_out);
  or or_15 (out_3[3], and_13_out, and_14_out);
  and and_14 (and_14_out, xor_8_out, not_22_out);
  and and_15 (and_15_out, or_13_out, or_12_out);
  or or_16 (or_16_out, and_15_out, and_16_out);
  and and_16 (and_16_out, not_23_out, not_24_out);
  not not_25 (not_25_out, in_1[4]);
  not not_26 (not_26_out, in_2[4]);
  not not_27 (not_27_out, xor_9_out);
  xor xor_9 (xor_9_out, in_2[4], in_1[4]);
  xor xor_10 (xor_10_out, in_2[4], in_1[4]);
  not not_28 (not_28_out, or_16_out);
  or or_17 (or_17_out, not_25_out, in_2[4]);
  not not_29 (not_29_out, or_18_out);
  or or_18 (or_18_out, in_1[4], not_26_out);
  not not_30 (not_30_out, or_16_out);
  and and_17 (and_17_out, not_27_out, or_16_out);
  and and_18 (and_18_out, xor_10_out, not_28_out);
  and and_19 (and_19_out, or_17_out, or_16_out);
  and and_20 (and_20_out, not_29_out, not_30_out);
  or or_19 (out_3[4], and_17_out, and_18_out);
  or or_20 (or_20_out, and_19_out, and_20_out);
  xor xor_11 (xor_11_out, in_2[5], in_1[5]);
  xor xor_12 (xor_12_out, in_2[5], in_1[5]);
  not not_31 (not_31_out, in_1[5]);
  or or_21 (or_21_out, not_31_out, in_2[5]);
  or or_22 (or_22_out, in_1[5], not_32_out);
  not not_32 (not_32_out, in_2[5]);
  not not_33 (not_33_out, xor_11_out);
  not not_34 (not_34_out, or_20_out);
  not not_35 (not_35_out, or_22_out);
  not not_36 (not_36_out, or_20_out);
  and and_21 (and_21_out, not_33_out, or_20_out);
  and and_22 (and_22_out, xor_12_out, not_34_out);
  and and_23 (and_23_out, or_21_out, or_20_out);
  and and_24 (and_24_out, not_35_out, not_36_out);
  or or_23 (out_3[5], and_21_out, and_22_out);
  or or_24 (or_24_out, and_23_out, and_24_out);
  not not_37 (not_37_out, in_1[6]);
  not not_38 (not_38_out, in_2[6]);
  xor xor_13 (xor_13_out, in_2[6], in_1[6]);
  xor xor_14 (xor_14_out, in_2[6], in_1[6]);
  or or_25 (or_25_out, not_37_out, in_2[6]);
  or or_26 (or_26_out, in_1[6], not_38_out);
  not not_39 (not_39_out, xor_13_out);
  and and_25 (and_25_out, not_39_out, or_24_out);
  and and_26 (and_26_out, xor_14_out, not_40_out);
  not not_40 (not_40_out, or_24_out);
  and and_27 (and_27_out, or_25_out, or_24_out);
  not not_41 (not_41_out, or_26_out);
  and and_28 (and_28_out, not_41_out, not_42_out);
  not not_42 (not_42_out, or_24_out);
  or or_27 (out_3[6], and_25_out, and_26_out);
  or or_28 (or_28_out, and_27_out, and_28_out);
  not not_43 (not_43_out, in_1[7]);
  not not_44 (not_44_out, in_2[7]);
  xor xor_15 (xor_15_out, in_2[7], in_1[7]);
  not not_45 (not_45_out, xor_15_out);
  xor xor_16 (xor_16_out, in_2[7], in_1[7]);
  not not_46 (not_46_out, or_28_out);
  or or_29 (or_29_out, not_43_out, in_2[7]);
  not not_47 (not_47_out, or_30_out);
  or or_30 (or_30_out, in_1[7], not_44_out);
  not not_48 (not_48_out, or_28_out);
  and and_29 (and_29_out, not_45_out, or_28_out);
  and and_30 (and_30_out, xor_16_out, not_46_out);
  and and_31 (and_31_out, or_29_out, or_28_out);
  and and_32 (and_32_out, not_47_out, not_48_out);
  or or_31 (out_3[7], and_29_out, and_30_out);
  // OR_Gate or_32 has open pins: in0=and_31_out, in4=and_32_out, out=open
endmodule
