// Logisim project D8421+1.circ as structural Verilog: 1 circuit, main circuit main
module main (
  input  [3:0] in_1,
  output [3:0] out_2
);

  wire and_1_out, and_2_out;

  not not_1 (out_2[0], in_1[0]);
  xor xor_1 (out_2[1], in_1[1], in_1[0]);
  and and_1 (and_1_out, in_1[1], in_1[0]);
  xor xor_2 (out_2[2], in_1[2], and_1_out);
  and and_2 (and_2_out, in_1[2], and_1_out);
  xor xor_3 (out_2[3], in_1[3], and_2_out);
endmodule
